// Logisim project ort_domaci_2.circ as structural Verilog: 1 circuit, main circuit main
module main (
  input  a,
  input  b,
  input  c,
  input  d,
  input  e,
  output x
);

  wire nor_1_out, nor_2_out, nor_3_out, nor_4_out, nor_5_out, nor_6_out, nor_7_out, nor_8_out;

  nor nor_1 (nor_1_out, b, b);
  nor nor_2 (nor_2_out, a, nor_1_out);
  nor nor_3 (nor_3_out, d, d);
  nor nor_4 (nor_4_out, nor_2_out, nor_2_out);
  nor nor_5 (nor_5_out, nor_4_out, c);
  nor nor_6 (nor_6_out, nor_3_out, e);
  nor nor_7 (nor_7_out, nor_5_out, nor_5_out);
  nor nor_8 (nor_8_out, nor_6_out, nor_6_out);
  nor nor_9 (x, nor_7_out, nor_8_out);

  // Notes on the sheet:
  //   Број: 10
  //   Датум рођења: 15.04
endmodule
